# Fritzing sketch fritzing (saved by Fritzing 0.9.5d)
breadboards: 1

parts:
  U1 = ESP32S-HiLetgo [part_number=ESP32S-HiLetgo]
  HC-SR04_Sensor_1 = HC-SR04 Ultrasonic Distance Sensor
  HC-SR04_Sensor_2 = HC-SR04 Ultrasonic Distance Sensor
  LED1 = LED - 3mm [color="Red (633nm)" package="3 mm [THT]"]
  LED2 = LED - 3mm [color="Red (633nm)" package="3 mm [THT]"]
  LED3 = LED - 3mm [color="Green (555nm)" package="3 mm [THT]"]
  LED4 = LED - 3mm [color="Green (555nm)" package="3 mm [THT]"]
  JACK1 = 2.1mm Barrel Jack with Terminal Block
  LCD2004-I2C1 = LCD2004-I2C
  J1 = Basic Servo
  J2 = Basic Servo
  S1 = Pushbutton [package="[SMD]"]
  S2 = Pushbutton [package="[SMD]"]
  M1 = IR break beam 3mm tx [package=THT]
  M2 = IR break beam 3mm rx [package=THT]
  M3 = IR break beam 3mm tx [package=THT]
  M4 = IR break beam 3mm rx [package=THT]
  R1 = Resistor [tolerance=±5% resistance=220 package="2010 [SMD]"]
  R2 = Resistor [tolerance=±5% resistance=220 package="2010 [SMD]"]
  R3 = Resistor [tolerance=±5% resistance=220 package="2010 [SMD]"]
  R4 = Resistor [tolerance=±5% resistance=220 package="2010 [SMD]"]
  R5 = Resistor [tolerance=±5% resistance=1k package="2010 [SMD]"]
  R6 = Resistor [tolerance=±5% resistance=2k package="2010 [SMD]"]
  R7 = Resistor [tolerance=±5% resistance=1k package="2010 [SMD]"]
  R8 = Resistor [tolerance=±5% resistance=2k package="2010 [SMD]"]

nets:
  N1: U1.3.3, R8.Pin_1
  N2: U1.GPIO32, S2.Pin_3, S2.Pin_4
  N3: U1.GPIO25, S1.Pin_3, S1.Pin_4
  N4: U1.GPIO26, M2.pin2
  N5: U1.GPIO27, R4.Pin_0
  N6: U1.GPIO14, R3.Pin_0
  N7: U1.GPIO12, R2.Pin_0
  GND: U1.GND, HC-SR04_Sensor_1.GND, HC-SR04_Sensor_2.GND, LED1.cathode, LED2.cathode, LED3.cathode, LED4.cathode, LCD2004-I2C1.GND, J1.gnd, J2.gnd, S1.Pin_1, S1.Pin_2, S2.Pin_1, S2.Pin_2, R6.Pin_0
  N8: U1.GPIO13, R1.Pin_0
  VCC: U1.VIN, HC-SR04_Sensor_1.VCC, HC-SR04_Sensor_2.VCC, LCD2004-I2C1.VCC, J1.vcc, J2.vcc
  N9: U1.GPIO4, R7.Pin_0, R8.Pin_0
  N10: U1.GPIO16, HC-SR04_Sensor_2.TRIG
  N11: U1.GPIO17, R5.Pin_0, R6.Pin_1
  N12: U1.GPIO5, HC-SR04_Sensor_1.TRIG
  N13: U1.GPIO18, J1.pulse
  N14: U1.GPIO19, J2.pulse
  N15: U1.GPIO21, LCD2004-I2C1.SDA
  N16: U1.GPIO22, LCD2004-I2C1.SCL
  N17: HC-SR04_Sensor_1.ECHO, R5.Pin_1
  N18: HC-SR04_Sensor_2.ECHO, R7.Pin_1
  N19: LED1.anode, R1.Pin_1
  N20: LED2.anode, R3.Pin_1
  N21: LED3.anode, R2.Pin_1
  N22: LED4.anode, R4.Pin_1
  N23: JACK1.POS, M1.pin1, M2.pin1, M3.pin1, M4.pin1
  N24: JACK1.NEG, M1.pin2, M2.pin3, M3.pin2, M4.pin3

notes:
  pintu masuk
  pintu keluar
  slot parkir 1
  slot parkir 2
  adaptor 12v 1A

custom parts:
  ESP32S-HiLetgo: HiLetgo ESP-WROOM-32 ESP32 ESP-32S Development Board 2.4GHz Dual-Mode WiFi + Bluetooth Dual Cores Microcontroller The ESP32 integrated with Antenna switches, RF Balun, power amplifiers, low-noise amplifiers, filters, and management modules, and the entire solution occupies the least area of PCB. 2.4 GHz Wi-Fi plus Bluetooth dual-mode chip, with TSMC Ultra-low power consumption 40nm technology,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
  LCD2004-I2C: A standard character display with 4x20 characters. Comes in many colors with LCM2004 IIC attached.
  IR break beam 3mm tx: Infrared break beam Sensor tx module.
  IR break beam 3mm rx: Infrared break beam Sensor rx module.
